// Logisim project ALU.circ as structural Verilog: 1 circuit, main circuit main
module main (
  input  [4:0] Shift,
  input  [3:0] Codop,
  input  [31:0] B,
  input  [31:0] A,
  input  Carryin,
  input  [31:0] in_6,
  output [3:0] Flags,
  output [31:0] S
);

  wire adder_1_cout, adder_2_cout, and_4_out, and_5_out, bitselector_1_out, bitselector_2_out,
       bitselector_3_out, bitselector_4_out, bitselector_5_out, bitselector_6_out, not_2_out, not_3_out,
       subtractor_1_bout, subtractor_3_bout, xor_2_out, xor_3_out;
  wire [4:0] adder_3_out, subtractor_4_out, subtractor_5_out, subtractor_6_out;
  wire [31:0] adder_1_out, adder_2_out, and_1_out, and_2_out, and_3_out, multiplier_1_out, not_1_out,
       or_1_out, shifter_1_out, shifter_2_out, shifter_3_out, shifter_4_out, subtractor_1_out,
       subtractor_2_out, subtractor_3_out, xor_1_out;

  assign not_1_out = ~B;  // NOT_Gate not_1, 32 bits wide
  assign and_1_out = A & B;  // AND_Gate and_1, 32 bits wide
  assign xor_1_out = A ^ B;  // XOR_Gate xor_1, 32 bits wide
  Shifter #(.width(32)) shifter_1 (.in(B), .\dist (Shift), .out(shifter_1_out));
  Shifter #(.width(32), .shift("lr")) shifter_2 (.in(B), .\dist (Shift), .out(shifter_2_out));
  Shifter #(.width(32), .shift("ar")) shifter_3 (.in(B), .\dist (Shift), .out(shifter_3_out));
  Adder #(.width(32)) adder_1 (.a(B), .b(A), .out(adder_1_out), .cin(Carryin), .cout(adder_1_cout));
  not not_2 (not_2_out, Carryin);
  Subtractor #(.width(32)) subtractor_1 (
    .a(A), .b(B), .out(subtractor_1_out), .bin(not_2_out), .bout(subtractor_1_bout));
  Shifter #(.width(32), .shift("rr")) shifter_4 (.in(B), .\dist (Shift), .out(shifter_4_out));
  assign and_2_out = B & A;  // AND_Gate and_2, 32 bits wide
  Subtractor #(.width(32)) subtractor_2 (.a(in_6), .b(B), .out(subtractor_2_out));  // open: bin, bout
  Subtractor #(.width(32)) subtractor_3 (.a(A), .b(B), .out(subtractor_3_out), .bout(subtractor_3_bout));  // open: bin
  Adder #(.width(32)) adder_2 (.a(A), .b(B), .out(adder_2_out), .cout(adder_2_cout));  // open: cin
  assign or_1_out = A | B;  // OR_Gate or_1, 32 bits wide
  Multiplier #(.width(32)) multiplier_1 (.b(B), .out(multiplier_1_out));  // open: a, cin, cout
  assign and_3_out = A & not_1_out;  // AND_Gate and_3, 32 bits wide
  Multiplexer #(.select(4), .width(32), .enable("false")) multiplexer_1 (
    .in0(and_1_out), .in1(xor_1_out), .in2(shifter_1_out), .in3(shifter_2_out), .in4(shifter_3_out),
    .in5(adder_1_out), .in6(subtractor_1_out), .in7(shifter_4_out), .in8(and_2_out), .in9(subtractor_2_out),
    .in10(subtractor_3_out), .in11(adder_2_out), .in12(or_1_out), .in13(multiplier_1_out), .in14(and_3_out),
    .in15(not_1_out), .out(S), .sel(Codop));
  Comparator #(.width(32)) comparator_1 (.a(S), .b({32{1'b0}}), .eq(Flags[1]), .lt(Flags[0]));  // open: gt
  Subtractor #(.width(5)) subtractor_4 (.a({5{1'b1}}), .b(Shift), .out(subtractor_4_out));  // open: bin, bout
  BitSelector #(.width(32)) bitselector_1 (.in(B), .out(bitselector_1_out), .sel(subtractor_5_out));
  Subtractor #(.width(5)) subtractor_5 (.a(Shift), .b(5'b00001), .out(subtractor_5_out));  // open: bin, bout
  BitSelector #(.width(32)) bitselector_2 (.in(B), .out(bitselector_2_out), .sel(subtractor_6_out));
  Subtractor #(.width(5)) subtractor_6 (.a(Shift), .b(5'b00001), .out(subtractor_6_out));  // open: bin, bout
  Adder #(.width(5)) adder_3 (.a(subtractor_4_out), .b({5{1'b1}}), .out(adder_3_out));  // open: cin, cout
  BitSelector #(.width(32)) bitselector_3 (.in(B), .out(bitselector_3_out), .sel(adder_3_out));
  Multiplexer #(.select(4), .enable("false")) multiplexer_2 (
    .in0(1'b0), .in1(1'b0), .in2(bitselector_3_out), .in3(bitselector_1_out), .in4(bitselector_2_out),
    .in5(adder_1_cout), .in6(subtractor_1_bout), .in7(Flags[0]), .in8(1'b0), .in9(1'b0),
    .in10(subtractor_3_bout), .in11(adder_2_cout), .in12(1'b0), .in13(1'b0), .in14(1'b0), .in15(1'b0),
    .out(Flags[2]), .sel(Codop));
  Multiplexer #(.select(4), .enable("false")) multiplexer_3 (
    .in0(1'b0), .in1(1'b0), .in2(1'b0), .in3(1'b0), .in4(1'b0), .in5(and_4_out), .in6(and_5_out), .in7(1'b0),
    .in8(1'b0), .in9(1'b0), .in10(and_5_out), .in11(and_4_out), .in12(1'b0), .in13(1'b0), .in14(1'b0),
    .in15(1'b0), .out(Flags[3]), .sel(Codop));
  BitSelector #(.width(32)) bitselector_4 (.in(B), .out(bitselector_4_out), .sel({5{1'b1}}));
  BitSelector #(.width(32)) bitselector_5 (.in(A), .out(bitselector_5_out), .sel({5{1'b1}}));
  BitSelector #(.width(32)) bitselector_6 (.in(S), .out(bitselector_6_out), .sel({5{1'b1}}));
  xor xor_2 (xor_2_out, bitselector_4_out, bitselector_5_out);
  xor xor_3 (xor_3_out, bitselector_5_out, bitselector_6_out);
  not not_3 (not_3_out, xor_2_out);
  and and_4 (and_4_out, not_3_out, xor_3_out);
  and and_5 (and_5_out, xor_2_out, xor_3_out);

  // Other names for the same wires on the sheet: N = Flags[0]; Z = Flags[1]; C = Flags[2]; V = Flags[3]; s0[31:0] = S;
  //   s1[31:0] = B; s2[31:0] = B; s3[31:0] = B
endmodule
