// Logisim project Flags_apsr.circ as structural Verilog: 1 circuit, main circuit main
module main (
  input  [3:0] in_1,
  input  [3:0] in_2,
  input  in_3,
  input  in_4,
  output [3:0] out_5
);

  wire [3:0] and_1_out, and_2_out, or_1_out;

  assign and_1_out = out_5 & ~in_1;  // AND_Gate and_1, 4 bits wide
  assign and_2_out = in_1 & in_2;  // AND_Gate and_2, 4 bits wide
  assign or_1_out = and_1_out | and_2_out;  // OR_Gate or_1, 4 bits wide
  Register #(.width(4)) register_1 (.D(or_1_out), .en(1'b1), .clk(in_3), .Q(out_5), .clr(in_4));
endmodule
