// Logisim project Machine.circ as structural Verilog: 2 circuits, main circuit main
module main (
  input  GPIO_A1,
  input  GPIO_A3,
  input  GPIO_A5,
  input  GPIO_A7,
  input  GPIO_A9,
  input  GPIO_A11,
  input  GPIO_A13,
  input  GPIO_A15,
  input  GPIO_A17,
  input  GPIO_A19,
  input  GPIO_A21,
  input  GPIO_A23,
  input  GPIO_A25,
  input  GPIO_A27,
  input  GPIO_A29,
  input  GPIO_A31,
  input  GPIO_A33,
  input  GPIO_A35,
  input  GPIO_B1,
  input  GPIO_B3,
  input  GPIO_B5,
  input  GPIO_B7,
  input  GPIO_B9,
  input  GPIO_B11,
  input  GPIO_B13,
  input  GPIO_B15,
  input  GPIO_B17,
  input  GPIO_B19,
  input  GPIO_B21,
  input  GPIO_B23,
  input  GPIO_B25,
  input  GPIO_B27,
  input  GPIO_B29,
  input  GPIO_B31,
  input  GPIO_B33,
  input  GPIO_B35,
  output GPIO_A2,
  output GPIO_A4,
  output GPIO_A6,
  output GPIO_A8,
  output GPIO_A10,
  output GPIO_A12,
  output GPIO_A14,
  output GPIO_A16,
  output GPIO_A18,
  output GPIO_A20,
  output GPIO_A22,
  output GPIO_A24,
  output GPIO_A26,
  output GPIO_A28,
  output GPIO_A30,
  output GPIO_A32,
  output GPIO_A34,
  output GPIO_A36,
  output GPIO_B2,
  output GPIO_B4,
  output GPIO_B6,
  output GPIO_B8,
  output GPIO_B10,
  output GPIO_B12,
  output GPIO_B14,
  output GPIO_B16,
  output GPIO_B18,
  output GPIO_B20,
  output GPIO_B22,
  output GPIO_B24,
  output GPIO_B26,
  output GPIO_B28,
  output GPIO_B30,
  output GPIO_B32,
  output GPIO_B34,
  output GPIO_B36
);

  wire Clk_Button_out, clock_1_out, CPU_1_store, Rst_Button_out;
  wire [7:0] RAM_Addr, ROM_Addr;
  wire [15:0] ROMa_data;
  wire [31:0] CPU_1_r0, CPU_1_r1, CPU_1_r2, CPU_1_r3, CPU_1_r4, CPU_1_r5, CPU_1_r6, CPU_1_r7, CPU_1_ram_out,
       RAMa_dout;
  wire [31:8] CPU_1_ram_addr;

  RAM #(.dataWidth(32), .databus("bibus")) RAMa (
    .addr(RAM_Addr), .we(CPU_1_store), .oe(1'b1), .clk(clock_1_out), .din(CPU_1_ram_out), .dout(RAMa_dout));
  Clock clock_1 (.out(clock_1_out));
  LED A0 (.in(RAMa_dout[0]));
  LED A1 (.in(RAMa_dout[1]));
  LED A2 (.in(RAMa_dout[2]));
  ROM #(.dataWidth(16)) ROMa (.addr(ROM_Addr), .data(ROMa_data));
  Button Clk_Button (.out(Clk_Button_out));
  Button Rst_Button (.out(Rst_Button_out));
  LED A3 (.in(RAMa_dout[3]));
  LED A4 (.in(RAMa_dout[4]));
  LED A5 (.in(RAMa_dout[5]));
  LED A6 (.in(RAMa_dout[6]));
  LED A7 (.in(RAMa_dout[7]));
  LED L0 (.in(CPU_1_r0[0]));
  // Probe on CPU_1_r1
  // Probe on CPU_1_r0
  LED L3 (.in(CPU_1_r0[3]));
  LED L1 (.in(CPU_1_r0[1]));
  LED L2 (.in(CPU_1_r0[2]));
  // Probe on CPU_1_r3
  // Probe on CPU_1_r2
  // Probe on CPU_1_r5
  // Probe on CPU_1_r4
  LED L4 (.in(CPU_1_r0[4]));
  LED L5 (.in(CPU_1_r0[5]));
  // Probe on CPU_1_r7
  // Probe on CPU_1_r6
  CPU CPU_1 (
    .ROM_Addr(ROM_Addr), .RAM_In(RAMa_dout), .R3(CPU_1_r3), .R7(CPU_1_r7), .R2(CPU_1_r2), .R6(CPU_1_r6),
    .RAM_Addr({CPU_1_ram_addr, RAM_Addr}), .R1(CPU_1_r1), .R5(CPU_1_r5), .ROM_In(ROMa_data), .R0(CPU_1_r0),
    .R4(CPU_1_r4), .Clk(clock_1_out), .RAM_Out(CPU_1_ram_out), .Reset(Rst_Button_out), .Store(CPU_1_store));
  LED L6 (.in(CPU_1_r0[6]));
  LED L7 (.in(CPU_1_r0[7]));
  LED LED_1 (.in(RAM_Addr[0]));
  LED LED_2 (.in(RAM_Addr[1]));
  LED LED_3 (.in(RAM_Addr[2]));
  LED LED_4 (.in(RAM_Addr[3]));
  LED LED_5 (.in(RAM_Addr[4]));
  LED LED_6 (.in(RAM_Addr[5]));
  LED LED_7 (.in(RAM_Addr[6]));
  LED LED_8 (.in(RAM_Addr[7]));

  // Notes on the sheet:
  //   contents of ROMa (hex, n*v repeats v):
  //   b08c 2000 9008 21ff 9104 9000 defe 9800 9904 4288 da08 defe 9800 9908 4081 9108 defe 9800 1c40 9000
  //   def0 b00c
  //   Use only 8 bit adresses
  //   VCC 5V
  //   VCC 3.3V
  //   VCC 5V
  //   VCC 3.3V
  //   GROUND
  //   GROUND
  //   GROUND
  //   GROUND
endmodule

module CPU (
  input  [31:0] RAM_In,
  input  [15:0] ROM_In,
  input  Clk,
  input  Reset,
  output [31:0] R3,
  output [31:0] R7,
  output [31:0] R2,
  output [31:0] R6,
  output [7:0] ROM_Addr,
  output [31:0] R1,
  output [31:0] R5,
  output [31:0] R0,
  output [31:0] R4,
  output [31:0] RAM_Addr,
  output [31:0] RAM_Out,
  output Store
);

  wire carry, imm32E, load, main_1_p14, MyController_p4, MyController_p16;
  wire [2:0] rd, RegA, RegB, regDest;
  wire [3:0] opcode;
  wire [4:0] imm5;
  wire [7:0] pc;
  wire [31:0] Aout, Bout, DataIn, imm32, multiplexer_2_out, multiplexer_3_out, ram_adr, sortieAlu;

  // Controller MyController: pin names not known; wires that end beside it: ROM_In, Clk, Reset, MyController_p4, pc, ram_adr, load, Store, imm32E, opcode, rd, RegA, RegB, imm32, imm5, MyController_p16
  Multiplexer #(.width(32), .enable("false")) multiplexer_1 (.in0(RAM_In), .in1(sortieAlu), .out(DataIn), .sel(load));
  Multiplexer #(.width(32), .enable("false")) multiplexer_2 (
    .in0(Aout), .in1(Bout), .out(multiplexer_2_out), .sel(MyController_p16));
  Multiplexer #(.width(32), .enable("false")) multiplexer_3 (
    .in0(Aout), .in1(imm32), .out(multiplexer_3_out), .sel(imm32E));
  // ALU MyAlu: pin names not known; wires that end beside it: multiplexer_2_out, multiplexer_3_out, opcode, carry, sortieAlu, Bout, MyController_p4
  Multiplexer #(.width(32), .enable("false")) multiplexer_4 (.in0(sortieAlu), .in1(Bout), .out(RAM_Out), .sel(Store));
  // MyBancDeRegistres_main main_1: pin names not known; wires that end beside it: R7, Reset, R6, RegA, R5, R4, Clk, R3, regDest, R2, RegB, R1, Aout, main_1_p14, DataIn, R0, main_1_p14, Bout
  // BancRegistre bancregistre_1: pin names not known

  // Other names for the same wires on the sheet: R1_t[31:0] = R0; R2_t[31:0] = R1; R3_t[31:0] = R2; R4_t[31:0] = R3;
  //   R5_t[31:0] = R4; R6_t[31:0] = R5; R7_t[31:0] = R6; R8[31:0] = R7; rst = Reset

  // Notes on the sheet:
  //   je n'ai pas réussi à modifier le circuit du banc de registre du coup il est moche
endmodule
