// Logisim project Load.circ as structural Verilog: 1 circuit, main circuit main
module main (
  input  Enable,
  input  [15:0] Instruction,
  input  Clk,
  input  Reset,
  input  [31:0] Stack_Pointer,
  output Store,
  output Load,
  output Pc_Hold,
  output [2:0] Rm,
  output [2:0] Rd,
  output [31:0] RAM_Addr
);

  wire and_2_out, d_ff_1_q, d_ff_1_qn, not_1_out, not_2_out;
  wire [15:0] and_1_out, bit_extender_1_out;
  wire [31:0] adder_1_out, bit_extender_2_out, bit_extender_3_out;

  assign bit_extender_1_out = {{15{Enable}}, Enable};  // Bit_Extender bit_extender_1
  assign {and_1_out[15:11], Rd, and_1_out[7:0]} = Instruction & bit_extender_1_out;  // AND_Gate and_1, 16 bits wide
  assign bit_extender_2_out = {{31{Enable}}, Enable};  // Bit_Extender bit_extender_2
  assign bit_extender_3_out = {{24{and_1_out[7]}}, and_1_out[7:0]};  // Bit_Extender bit_extender_3
  Adder #(.width(32)) adder_1 (.a(bit_extender_3_out), .b(Stack_Pointer), .out(adder_1_out));  // open: cin, cout
  D_Flip_Flop d_ff_1 (.D(and_2_out), .clk(Clk), .Q(d_ff_1_q), .Qn(d_ff_1_qn), .preset(1'b0), .reset(Reset));
  and and_2 (and_2_out, d_ff_1_qn, Enable);
  assign RAM_Addr = adder_1_out & bit_extender_2_out;  // AND_Gate and_3, 32 bits wide
  and and_4 (Store, Enable, not_1_out, d_ff_1_qn);
  not not_1 (not_1_out, and_1_out[11]);
  and and_5 (Load, and_1_out[11], d_ff_1_q);
  not not_2 (not_2_out, d_ff_1_q);
  and and_6 (Pc_Hold, not_2_out, Enable);

  assign Rm = Rd;
endmodule
