// Logisim project Data_Processing.circ as structural Verilog: 1 circuit, main circuit main
module main (
  input  [15:0] in_1,
  input  in_2,
  output [2:0] out_3,
  output [2:0] out_4,
  output [2:0] out_5,
  output [3:0] out_6,
  output [3:0] out_7
);

  wire [5:0] bitselector_1_out;
  wire [15:0] and_1_out, bit_extender_1_out;

  assign bit_extender_1_out = {{15{in_2}}, in_2};  // Bit_Extender bit_extender_1
  assign and_1_out = in_1 & bit_extender_1_out;  // AND_Gate and_1, 16 bits wide
  BitSelector #(.width(16), .group(6)) bitselector_1 (.in(and_1_out), .out(bitselector_1_out), .sel(2'b01));
  BitSelector #(.width(16), .group(3)) bitselector_2 (.in(and_1_out), .out(out_3), .sel(3'b000));
  BitSelector #(.width(16), .group(3)) bitselector_3 (.in(and_1_out), .out(out_5), .sel(3'b001));
  BitSelector #(.width(6), .group(4)) bitselector_4 (.in(bitselector_1_out), .out(out_7), .sel(1'b0));
  Multiplexer #(.select(4), .width(4), .enable("false")) multiplexer_1 (
    .in0(4'b1110), .in1(4'b1110), .in2(4'b1110), .in3(4'b1110), .in4(4'b1110), .in5(4'b1111), .in6(4'b1111),
    .in7(4'b1110), .in8(4'b1110), .in9(4'b1111), .in10(4'b1111), .in11(4'b1111), .in12(4'b1110),
    .in13(4'b1100), .in14(4'b1110), .in15(4'b1110), .out(out_6), .sel(out_7));

  assign out_4 = out_3;

  // Notes on the sheet:
  //   Pull output low on Enable = 0
  //   Note 2: RSB instruction has Rn as 1st operand.
  //   MUL instruction has Rn as 1st operand and Rdm as 2nd operand
  //   For simplification purposes, Rm is used for 1st operand both here and in the ALU.
  //   Note: instructions that does not save the result will still have the second operand as the destination register, the ALU will copy the second register to the destination register
endmodule
