// Logisim project Opcode.circ as structural Verilog
module Controleur (
  input  [5:0] Opcode,
  output Shift,
  output DataProcessing,
  output LoadStore,
  output SPAdress,
  output Branch
);

  wire not_1_out, not_2_out, not_3_out, not_4_out, not_5_out, not_6_out, not_7_out, not_8_out, not_9_out,
       not_10_out, not_11_out;

  not not_1 (not_1_out, Opcode[4]);
  and and_1 (Shift, not_1_out, not_2_out);
  not not_2 (not_2_out, Opcode[5]);
  not not_3 (not_3_out, Opcode[5]);
  not not_4 (not_4_out, Opcode[3]);
  and and_2 (DataProcessing, not_3_out, Opcode[4], not_4_out, not_5_out, not_6_out, not_7_out);
  not not_5 (not_5_out, Opcode[2]);
  not not_6 (not_6_out, Opcode[1]);
  not not_7 (not_7_out, Opcode[0]);
  not not_8 (not_8_out, Opcode[4]);
  and and_3 (LoadStore, Opcode[5], not_8_out, not_9_out, Opcode[2]);
  not not_9 (not_9_out, Opcode[3]);
  not not_10 (not_10_out, Opcode[4]);
  and and_4 (SPAdress, Opcode[5], not_10_out, Opcode[3], Opcode[2]);
  and and_5 (Branch, Opcode[5], Opcode[4], not_11_out, Opcode[2]);
  not not_11 (not_11_out, Opcode[3]);
endmodule
