// Logisim project banc_saveAB_reset.circ as structural Verilog: 1 circuit, main circuit main
module main (
  input  [31:0] Dataln,
  input  in_2,
  input  [2:0] RegB,
  input  [2:0] RegDest,
  input  Clk,
  input  in_6,
  input  [2:0] in_7,
  input  [2:0] RegA,
  input  [2:0] in_9,
  input  in_10,
  output [31:0] Bout,
  output [31:0] Aout
);

  wire R0, R1, R2, R3, R4, R5, R6, R7, undriven;
  wire [31:0] B1, B2, B3, B4, B5, B6, B7, B8, D0, D1, D2, D3, D4, D5, D6, D7, multiplexer_2_out,
       multiplexer_3_out;

  Demultiplexer #(.select(3), .width(32), .enable("false")) demultiplexer_1 (
    .out0(D0), .out1(D1), .out2(D2), .out3(D3), .out4(D4), .out5(D5), .out6(D6), .out7(D7), .in(Dataln),
    .sel(RegDest));
  Multiplexer #(.select(3), .width(3)) multiplexer_1 ();  // open: in0, in1, in2, in3, in4, in5, in6, in7, out, sel, en
  Decoder #(.select(3)) decoder_1 (
    .out0(R0), .out1(R1), .out2(R2), .out3(R3), .out4(R4), .out5(R5), .out6(R6), .out7(R7), .sel(RegDest));  // open: en
  Register #(.width(32)) u_R0 (.D(D0), .en(R0), .clk(Clk), .Q(B1), .clr(in_10));
  Register #(.width(32)) u_R1 (.D(D1), .en(R1), .clk(Clk), .Q(B2), .clr(in_10));
  Register #(.width(32)) u_R2 (.D(D2), .en(R2), .clk(Clk), .Q(B3), .clr(in_10));
  Register #(.width(32)) u_R3 (.D(D3), .en(R3), .clk(Clk), .Q(B4), .clr(in_10));
  Register #(.width(32)) u_R4 (.D(D4), .en(R4), .clk(Clk), .Q(B5), .clr(in_10));
  Register #(.width(32)) u_R5 (.D(D5), .en(R5), .clk(Clk), .Q(B6), .clr(in_10));
  Register #(.width(32)) u_R6 (.D(D6), .en(R6), .clk(Clk), .Q(B7), .clr(in_10));
  Register #(.width(32)) u_R7 (.D(D7), .en(R7), .clk(Clk), .Q(B8), .clr(in_10));
  Multiplexer #(.select(3), .width(32)) multiplexer_2 (
    .in0(B1), .in1(B2), .in2(B3), .in3(B4), .in4(B5), .in5(B6), .in6(B7), .in7(B8), .out(multiplexer_2_out),
    .sel(RegA), .en(undriven));
  Register #(.width(32)) register_1 (.D(multiplexer_2_out), .en(in_6), .clk(Clk), .Q(Aout));  // open: clr
  Multiplexer #(.select(3), .width(32), .enable("false")) multiplexer_3 (
    .in0(B1), .in1(B2), .in2(B3), .in3(B4), .in4(B5), .in5(B6), .in6(B7), .in7(B8), .out(multiplexer_3_out),
    .sel(RegB));
  Register #(.width(32)) register_2 (.D(multiplexer_3_out), .en(in_2), .clk(Clk), .Q(Bout));  // open: clr

  // Other names for the same wires on the sheet: Re1 = in_10; Re2 = in_10; Re3 = in_10; Re4 = in_10; Re5 = in_10;
  //   Re6 = in_10; Re7 = in_10; Re8 = in_10
endmodule
