// Logisim project sp_adresse.circ as structural Verilog: 1 circuit, main circuit main
// Data
module main (
  input  [15:0] Inst,
  input  [31:0] Stack_Pointer,
  input  Enable,
  input  Write_Enable,
  output [31:0] out_5
);

  wire A1, priority_encoder_1_out;
  wire [6:0] bitselector_1_out;
  wire [31:0] adder_1_out, bit_extender_1_out, subtractor_1_out;

  BitSelector #(.width(16), .group(7)) bitselector_1 (.in(Inst), .out(bitselector_1_out), .sel(2'b00));
  assign bit_extender_1_out = {{25{bitselector_1_out[6]}}, bitselector_1_out};  // Bit_Extender bit_extender_1
  not not_1 (A1, Inst[7]);
  Adder #(.width(32)) adder_1 (.a(bit_extender_1_out), .b(Stack_Pointer), .out(adder_1_out));  // open: cin, cout
  Subtractor #(.width(32)) subtractor_1 (
    .a(Stack_Pointer), .b(bit_extender_1_out), .out(subtractor_1_out));  // open: bin, bout
  Multiplexer #(.width(32), .enable("false")) multiplexer_1 (
    .in0(adder_1_out), .in1(subtractor_1_out), .out(out_5), .sel(priority_encoder_1_out));
  Priority_Encoder #(.select(1)) priority_encoder_1 (
    .in0(A1), .in1(Inst[7]), .out(priority_encoder_1_out));  // open: gs, en_out, en_in

  assign Write_Enable = Enable;

  // Other names for the same wires on the sheet: A2 = Inst[7]
endmodule
