// Logisim project shif_add_sub_remove.circ as structural Verilog: 1 circuit, main circuit main
module main (
  input  [15:0] Instruction,
  input  Enable,
  output [3:0] ALU_Opcode,
  output [4:0] Imm5,
  output [2:0] Rd,
  output [2:0] Rn,
  output [2:0] Rm,
  output [3:0] Flags_Update_Mask,
  output Imm32_Enable,
  output Carry,
  output [31:0] Imm32
);

  wire E1, E2, E3, E4, E5, E6, E7, E8, not_1_out, not_2_out, not_3_out, not_4_out, not_5_out, not_6_out,
       not_7_out, not_8_out, not_9_out, not_10_out, not_11_out, not_12_out, not_13_out, not_14_out,
       not_15_out, or_1_out, or_2_out, or_3_out, priority_encoder_1_out, priority_encoder_3_out,
       priority_encoder_4_out;
  wire [2:0] bitselector_6_out, bitselector_7_out, priority_encoder_2_out, priority_encoder_5_out, RDDebut,
       RDFin, RMDeb, RMFin;
  wire [4:0] bitselector_8_out;
  wire [5:0] bitselector_11_out;
  wire [7:0] bitselector_3_out, bitselector_4_out;
  wire [8:0] bitselector_1_out, bitselector_2_out;
  wire [15:0] and_1_out, bit_extender_1_out;
  wire [31:0] bit_extender_2_out, bit_extender_3_out, multiplexer_1_out;

  assign bit_extender_1_out = {{15{Enable}}, Enable};  // Bit_Extender bit_extender_1
  assign and_1_out = Instruction & bit_extender_1_out;  // AND_Gate and_1, 16 bits wide
  BitSelector #(.width(16), .group(9)) bitselector_1 (.in(and_1_out), .out(bitselector_1_out), .sel(1'b0));
  BitSelector #(.width(16), .group(9)) bitselector_2 (.in(and_1_out), .out(bitselector_2_out), .sel(1'b1));
  BitSelector #(.width(16), .group(8)) bitselector_3 (.in(and_1_out), .out(bitselector_3_out), .sel(1'b0));
  BitSelector #(.width(16), .group(8)) bitselector_4 (.in(and_1_out), .out(bitselector_4_out), .sel(1'b1));
  BitSelector #(.group(3)) bitselector_5 (.in(bitselector_4_out), .out(RDDebut), .sel(2'b00));
  BitSelector #(.group(3)) bitselector_6 (.in(bitselector_4_out), .out(bitselector_6_out), .sel(2'b01));
  BitSelector #(.group(3)) bitselector_7 (.in(and_1_out[15:8]), .out(bitselector_7_out), .sel(2'b01));
  BitSelector #(.width(9), .group(5)) bitselector_8 (.in(bitselector_2_out), .out(bitselector_8_out), .sel(1'b0));
  not not_1 (not_1_out, bitselector_7_out[0]);
  not not_2 (not_2_out, bitselector_7_out[1]);
  not not_3 (not_3_out, bitselector_7_out[2]);
  not not_4 (not_4_out, bitselector_7_out[2]);
  not not_5 (not_5_out, bitselector_7_out[1]);
  not not_6 (not_6_out, bitselector_7_out[2]);
  not not_7 (not_7_out, bitselector_7_out[0]);
  not not_8 (not_8_out, bitselector_7_out[2]);
  BitSelector #(.width(9), .group(3)) bitselector_9 (.in(bitselector_1_out), .out(Rn), .sel(2'b01));
  BitSelector #(.width(9), .group(3)) bitselector_10 (.in(bitselector_1_out), .out(RMDeb), .sel(2'b10));
  not not_9 (not_9_out, bitselector_6_out[0]);
  not not_10 (not_10_out, bitselector_6_out[1]);
  and and_2 (E1, not_1_out, not_2_out, not_3_out);
  and and_3 (E2, not_4_out, not_5_out, bitselector_7_out[0]);
  and and_4 (E3, not_6_out, bitselector_7_out[1], not_7_out);
  and and_5 (E4, not_8_out, bitselector_7_out[1], bitselector_7_out[0]);
  not not_11 (not_11_out, bitselector_8_out[4]);
  and and_6 (E8, not_9_out, not_10_out, bitselector_6_out[2]);
  not not_12 (not_12_out, bitselector_8_out[1]);
  not not_13 (not_13_out, bitselector_8_out[0]);
  not not_14 (not_14_out, bitselector_8_out[4]);
  not not_15 (not_15_out, bitselector_8_out[4]);
  and and_7 (E5, bitselector_8_out[0], not_12_out, bitselector_8_out[2], bitselector_8_out[3], not_11_out);
  and and_8 (E6, not_13_out, bitselector_8_out[1], bitselector_8_out[2], bitselector_8_out[3], not_14_out);
  and and_9 (E7, bitselector_8_out[0], bitselector_8_out[1], bitselector_8_out[2], bitselector_8_out[3], not_15_out);
  BitSelector #(.width(16), .group(6)) bitselector_11 (.in(and_1_out), .out(bitselector_11_out), .sel(2'b01));
  BitSelector #(.width(6), .group(5)) bitselector_12 (.in(bitselector_11_out), .out(Imm5), .sel(1'b0));
  BitSelector #(.width(16), .group(3)) bitselector_13 (.in(and_1_out), .out(RDFin), .sel(3'b000));
  BitSelector #(.width(16), .group(3)) bitselector_14 (.in(and_1_out), .out(RMFin), .sel(3'b001));
  assign bit_extender_2_out = {{24{bitselector_3_out[7]}}, bitselector_3_out};  // Bit_Extender bit_extender_2
  assign bit_extender_3_out = {{29{RMDeb[2]}}, RMDeb};  // Bit_Extender bit_extender_3
  Multiplexer #(.width(32), .enable("false")) multiplexer_1 (
    .in0(bit_extender_2_out), .in1(bit_extender_3_out), .out(multiplexer_1_out), .sel(priority_encoder_1_out));
  Priority_Encoder #(.select(1)) priority_encoder_1 (
    .in0(E8), .in1(E7), .out(priority_encoder_1_out));  // open: gs, en_out, en_in
  or or_1 (or_1_out, E1, E2, E3, E4, E5, E6, E7);
  or or_2 (or_2_out, E1, E2, E3);
  or or_3 (or_3_out, E4, E5);
  Priority_Encoder priority_encoder_2 (
    .in0(E1), .in1(E2), .in2(E3), .in3(E4), .in4(E5), .in5(E6), .in6(E7), .in7(E8),
    .out(priority_encoder_2_out), .en_in(1'b1));  // open: gs, en_out
  Multiplexer #(.width(3), .enable("false")) multiplexer_2 (
    .in0(RDFin), .in1(RDDebut), .out(Rd), .sel(priority_encoder_3_out));
  Priority_Encoder #(.select(1)) priority_encoder_3 (
    .in0(or_1_out), .in1(E8), .out(priority_encoder_3_out));  // open: gs, en_out, en_in
  or or_4 (Imm32_Enable, E8, E4, E5);
  Multiplexer #(.select(3), .width(4), .enable("false")) multiplexer_3 (
    .in0(4'b0000), .in1(4'b0001), .in2(4'b0010), .in3(4'b0011), .in4(4'b0100), .in5(4'b0101), .in6(4'b0110),
    .in7(4'b0111), .out(ALU_Opcode), .sel(priority_encoder_2_out));
  Multiplexer #(.width(3), .enable("false")) multiplexer_4 (
    .in0(RMFin), .in1(RMDeb), .out(Rm), .sel(priority_encoder_4_out));
  Priority_Encoder #(.select(1)) priority_encoder_4 (
    .in0(or_2_out), .in1(or_3_out), .out(priority_encoder_4_out));  // open: gs, en_out, en_in
  or or_5 (Carry, E4, E5);
  Multiplexer #(.select(3), .width(4), .enable("false")) multiplexer_5 (
    .in0(4'b1110), .in1(4'b1110), .in2(4'b1110), .in3(4'b1111), .in4(4'b1111), .in5(4'b1111), .in6(4'b1111),
    .in7(4'b1100), .out(Flags_Update_Mask), .sel(priority_encoder_5_out));
  Priority_Encoder priority_encoder_5 (
    .in0(E1), .in1(E2), .in2(E3), .in3(E4), .in4(E5), .in5(E6), .in6(E7), .out(priority_encoder_5_out),
    .en_in(1'b1));  // open: in7, gs, en_out

  // Other names for the same wires on the sheet: O1 = E1; O2 = E2; O3 = E3; O4 = E4; O5 = E5; O6 = E6; O7 = E7;
  //   O8 = E8

  // Notes on the sheet:
  //   Pull output low on Enable = 0
  //   Note 3: Imm32_Enable forces the use of the immediate for Rm register
  //   Note: ALU uses Rn register for shifts. Use Rn instead of Rm for shifts (immediate) here too
  //   Note 2: MOV uses RSB ALU opcode with Imm8 reversed so that it is copied to output register
  //   IMM8 
  //   RD
  //   Add register
  //   Logical Shift Left
  //   Logical Shift Right
  //   Arithmetic Shift Right
  //   MOVE
  //   Pull output low on Enable = 0
  //   Substract Register
  //   Add 3-bit Immediate
  //   RD
  //   RM
  //   RN
  //   RM / IMM3
  //   ALU will use Imm32 instead of Rm
  //   Enable carry for SUB since it is reversed in ALU
  //   Note 3: Imm32_Enable forces the use of the immediate for Rm register
  //   Note: ALU uses Rn register for shifts. Use Rn instead of Rm for shifts (immediate) here too
  //   Note 2: MOV uses RSB ALU opcode with Imm8 reversed so that it is copied to output register
  //   Enable carry for SUB since it is reversed in ALU
  //   ALU will use Imm32 instead of Rm
endmodule
